# Fritzing sketch ESP_BLUETHOOT (saved by Fritzing 0.9.3b)

parts:
  Part2 = Adafruit MAX98357A I2S 3W Class D Amplifier [part_number="Adafruit #3006"]
  U1 = LuaNode32 / ESP32 [part_number=ESP32S-PIN30]

nets:
  VIN: Part2.VIN, U1.Vin
  GND: Part2.GND, U1.GND
  N1: Part2.DIN, U1.D25
  N2: Part2.BCLK, U1.D27
  N3: Part2.LRCLK, U1.D26

custom parts:
  Adafruit MAX98357A I2S 3W Class D Amplifier: Listen to this good news - we now have an all in one digital audio amp breakout board that works incredibly well with the Raspberry Pi! If you're looking for an easy and low cost way to get you digital sound files bumpin' then the MAX08357 I2S Amp Breakout is for you. It takes standard I2S digital audio input and, not only decodes it into analog, but also amplifies it directly into a speaker.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
  LuaNode32 / ESP32: New Image for LuaNode32 DOIT ESP32 DEVKIT V1. Base parts from LuaNode32 / ESP32 ESP32 based LuaNode32 by G.Noorlander DOIT Esp32 DevKit v1 (30 pins long, 11 pins width) by Werner Rothschopf (modified by vanepp Dec 2018)
